# Fritzing sketch wiring (saved by Fritzing 0.9.3b)

parts:
  Součástka1 = Arduino Uno (Rev3)
  Součástka2 = Arduino Uno (Rev3)
  Součástka3 = Arduino Nano (Rev3.0)
  RS485_module1 = RS485 Module (MAX3485)
  RS485_module2 = RS485 Module (MAX3485)
  RS485_module3 = RS485 Module (MAX3485)

nets:
  N1: Součástka1.D8, RS485_module3.RO
  N2: Součástka1.D9_PWM, RS485_module3.DI
  GND: Součástka1.GND, RS485_module3.GND
  N3: Součástka1.D7, RS485_module3.RE, RS485_module3.DE
  5V: Součástka1.5V, RS485_module3.VCC
  N4: Součástka2.D8, RS485_module1.RO
  N5: Součástka2.D9_PWM, RS485_module1.DI
  GND_2: Součástka2.GND, RS485_module1.GND
  N6: Součástka2.D7, RS485_module1.RE, RS485_module1.DE
  5V_2: Součástka2.5V, RS485_module1.VCC
  N7: Součástka3.D7, RS485_module2.RE, RS485_module2.DE
  N8: Součástka3.D8, RS485_module2.RO
  N9: Součástka3.D9, RS485_module2.DI
  GND_3: Součástka3.GND, RS485_module2.GND
  5V_3: Součástka3.5V, RS485_module2.VCC
  N10: RS485_module1.A, RS485_module2.A, RS485_module3.A
  N11: RS485_module1.B, RS485_module2.B, RS485_module3.B

custom parts:
  RS485 Module (MAX3485): Commercially available RS485 to RS232 TTL Module
